# Fritzing sketch robot (saved by Fritzing 0.9.3b)

parts:
  J2 = Infrared Proximity Sensor
  J3 = Infrared Proximity Sensor
  J4 = Basic Servo
  M1 = DC Motor
  VCC1 = Battery
  Power_plug1 = Power plug
  Часть1 = Arduino Nano (Rev3.0)
  U1 = SWITCH_SPDT [package=kps-1290]
  U2 = SWITCH_SPDT [package=kps-1290]
  M2 = DC Motor
  S1 = H-Bridge with L298N
  J5 = Infrared Proximity Sensor

nets:
  N1: J2.Vout, Часть1.A1
  N2: J3.Vout, Часть1.A2
  N3: J4.pulse, Часть1.D10
  N4: M1.pin_1, S1.M1-02
  N5: M1.pin_2, S1.M1-01
  N6: VCC1.-, Power_plug1.GND
  N7: VCC1.+, Power_plug1.VCC
  N8: Часть1.D4, S1.IN4
  N9: Часть1.D5, S1.IN3
  N10: Часть1.D6, S1.IN2
  N11: Часть1.D7, S1.IN1
  N12: Часть1.VIN, U2.P
  N13: Часть1.A0, J5.Vout
  N14: U1.S, S1.12V
  N15: M2.pin_1, S1.M2-01
  N16: M2.pin_2, S1.M2-02
  N17: S1.ENA, S1.ENA-5V
  N18: S1.ENB, S1.ENB-5V

custom parts:
  H-Bridge with L298N: h-bridge
